// Logisim project ISA.circ as structural Verilog: 4 circuits, main circuit ULA
module Main (
);

  wire and_1_out, Branch, CLK, comparator_1_eq, comparator_2_eq, comparator_3_eq, comparator_4_eq,
       comparator_4_gt, comparator_5_lt, Mem_read, Mem_write, MemToReg, multiplexer_7_out, not_1_out,
       or_1_out, RegWrite, ULAsrc;
  wire [1:0] BranchType, FUNCT, RD, RS1, RS2;
  wire [3:0] Funct_data, multiplexer_5_out, OPCODE, ULA_CONTROL;
  wire [5:2] IMM;
  wire [11:0] adder_1_out, adder_2_out, b_reg_1_saida_1, b_reg_1_saida_2, bit_extender_1_out,
       bit_extender_2_out, MDATA_dout, multiplexer_1_out, multiplexer_4_out, multiplexer_6_out, PC_q,
       ula_1_saida;

  assign bit_extender_1_out = {{8{IMM[3]}}, {IMM[3:2], FUNCT}};  // Bit_Extender bit_extender_1
  Adder #(.width(12)) adder_1 (.a(PC_q), .b(bit_extender_1_out), .out(adder_1_out));  // open: cin, cout
  Register #(.width(12)) PC (.D(multiplexer_1_out), .en(CLK), .clk(CLK), .Q(PC_q));  // open: clr
  Multiplexer #(.width(12)) multiplexer_1 (
    .in0(adder_2_out), .in1(adder_1_out), .out(multiplexer_1_out), .sel(and_1_out));
  Clock clock_1 (.out(CLK));
  Adder #(.width(12)) adder_2 (.a(PC_q), .b(12'h1), .out(adder_2_out));  // open: cin, cout
  ROM #(.addrWidth(12), .dataWidth(12)) MINS (.addr(PC_q), .data({OPCODE, RD, IMM, FUNCT}));
  ROM #(.addrWidth(4), .dataWidth(12)) UCONTROL (
    .addr(OPCODE), .data({RegWrite, MemToReg, Mem_read, Mem_write, BranchType, Branch, ULAsrc, ULA_CONTROL}));
  Multiplexer #(.width(2)) multiplexer_2 (.in0(IMM[5:4]), .in1(RD), .out(RS1), .sel(Branch));
  Multiplexer #(.width(2)) multiplexer_3 (.in0(IMM[3:2]), .in1(IMM[5:4]), .out(RS2), .sel(Branch));
  B_REG b_reg_1 (
    .DATA(multiplexer_6_out), .RegWrite(RegWrite), .CLK(CLK), .RD(RD), .RS1(RS1), .RS2(RS2),
    .SAIDA_1(b_reg_1_saida_1), .SAIDA_2(b_reg_1_saida_2));
  assign bit_extender_2_out = {{6{IMM[5]}}, {IMM, FUNCT}};  // Bit_Extender bit_extender_2
  ROM #(.addrWidth(2), .dataWidth(4)) u_Funct (.addr(FUNCT), .data(Funct_data));
  RAM #(.addrWidth(12), .dataWidth(12)) MDATA (
    .addr(ula_1_saida), .we(Mem_write), .oe(Mem_read), .clk(CLK), .din(b_reg_1_saida_2), .dout(MDATA_dout));
  Multiplexer #(.width(12)) multiplexer_4 (
    .in0(b_reg_1_saida_2), .in1(bit_extender_2_out), .out(multiplexer_4_out), .sel(ULAsrc));
  Multiplexer #(.width(4)) multiplexer_5 (
    .in0(ULA_CONTROL), .in1(Funct_data), .out(multiplexer_5_out), .sel(comparator_1_eq));
  ULA ula_1 (.rs1(b_reg_1_saida_1), .rs2(multiplexer_4_out), .ULA_CONTROL(multiplexer_5_out), .SAIDA(ula_1_saida));
  Comparator #(.width(4)) comparator_1 (.a(ULA_CONTROL), .b(4'b0111), .eq(comparator_1_eq));  // open: gt, lt
  Comparator #(.width(12)) comparator_2 (
    .a(b_reg_1_saida_1), .b(b_reg_1_saida_2), .eq(comparator_2_eq));  // open: gt, lt
  Comparator #(.width(12)) comparator_3 (
    .a(b_reg_1_saida_1), .b(b_reg_1_saida_2), .eq(comparator_3_eq));  // open: gt, lt
  Comparator #(.width(12)) comparator_4 (
    .a(b_reg_1_saida_1), .b(b_reg_1_saida_2), .gt(comparator_4_gt), .eq(comparator_4_eq));  // open: lt
  Comparator #(.width(12)) comparator_5 (
    .a(b_reg_1_saida_1), .b(b_reg_1_saida_2), .lt(comparator_5_lt));  // open: gt, eq
  Multiplexer #(.width(12)) multiplexer_6 (
    .in0(ula_1_saida), .in1(MDATA_dout), .out(multiplexer_6_out), .sel(MemToReg));
  not not_1 (not_1_out, comparator_3_eq);
  or or_1 (or_1_out, comparator_4_gt, comparator_4_eq);
  and and_1 (and_1_out, Branch, multiplexer_7_out);
  Multiplexer #(.select(2)) multiplexer_7 (
    .in0(comparator_2_eq), .in1(not_1_out), .in2(or_1_out), .in3(comparator_5_lt), .out(multiplexer_7_out),
    .sel(BranchType));

  // Other names for the same wires on the sheet: IMM[1:0] = FUNCT; IMM_B[3:0] = {IMM[3:2], FUNCT}

  // Notes on the sheet:
  //   contents of UCONTROL (hex, n*v repeats v):
  //   3e0 250 2f0 210 230 270 310 330 25a 54 c1 c1 251 0 0 201
  //   contents of Funct (hex, n*v repeats v):
  //   2 6 0 7
endmodule

module ULA (
  input  [11:0] rs1,
  input  [11:0] rs2,
  input  [3:0] ULA_CONTROL,
  output [11:0] SAIDA
);

  wire comparator_1_lt;
  wire [11:0] adder_1_out, and_1_out, bit_extender_1_out, not_1_out, or_1_out, shifter_1_out, shifter_2_out,
       subtractor_1_out, xor_1_out;

  Adder #(.width(12)) adder_1 (.a(rs1), .b(rs2), .out(adder_1_out));  // open: cin, cout
  Subtractor #(.width(12)) subtractor_1 (.a(rs1), .b(rs2), .out(subtractor_1_out));  // open: bin, bout
  Shifter #(.width(12)) shifter_1 (.in(rs1), .\dist (4'b0001), .out(shifter_1_out));
  Shifter #(.shift("lr"), .width(12)) shifter_2 (.in(rs1), .\dist (4'b0001), .out(shifter_2_out));
  assign and_1_out = rs1 & rs2;  // AND_Gate and_1, 12 bits wide
  assign or_1_out = rs1 | rs2;  // OR_Gate or_1, 12 bits wide
  assign xor_1_out = rs1 ^ rs2;  // XOR_Gate xor_1, 12 bits wide
  assign not_1_out = ~rs1;  // NOT_Gate not_1, 12 bits wide
  Comparator #(.width(12)) comparator_1 (.a(rs1), .b(rs2), .lt(comparator_1_lt));  // open: gt, eq
  assign bit_extender_1_out = {{11{comparator_1_lt}}, comparator_1_lt};  // Bit_Extender bit_extender_1
  Multiplexer #(.select(4), .width(12)) multiplexer_1 (
    .in0(adder_1_out), .in1(subtractor_1_out), .in2(shifter_1_out), .in3(shifter_2_out), .in4(and_1_out),
    .in5(or_1_out), .in6(xor_1_out), .in7(not_1_out), .in8(bit_extender_1_out), .out(SAIDA), .sel(ULA_CONTROL));  // open: in9, in10, in11, in12, in13, in14, in15
endmodule

module B_REG (
  input  [11:0] DATA,
  input  RegWrite,
  input  CLK,
  input  [1:0] RD,
  input  [1:0] RS1,
  input  [1:0] RS2,
  output [11:0] SAIDA_1,
  output [11:0] SAIDA_2
);

  wire and_1_out, and_2_out, and_3_out, and_4_out, decoder_1_out0, decoder_1_out1, decoder_1_out2,
       decoder_1_out3;
  wire [11:0] R0, R1, R2, R3, undriven;

  Decoder #(.select(2)) decoder_1 (
    .out0(decoder_1_out0), .out1(decoder_1_out1), .out2(decoder_1_out2), .out3(decoder_1_out3), .sel(RD));  // open: en
  and and_1 (and_1_out, decoder_1_out0, RegWrite);
  and and_2 (and_2_out, decoder_1_out3, RegWrite);
  and and_3 (and_3_out, decoder_1_out1, RegWrite);
  and and_4 (and_4_out, decoder_1_out2, RegWrite);
  Register #(.width(12)) register_1 (.D(undriven), .en(and_1_out), .Q(R0));  // open: clk, clr
  Register #(.width(12)) register_2 (.D(undriven), .en(and_4_out), .Q(R2));  // open: clk, clr
  Register #(.width(12)) register_3 (.D(undriven), .en(and_3_out), .Q(R1));  // open: clk, clr
  Register #(.width(12)) register_4 (.D(undriven), .en(and_2_out), .Q(R3));  // open: clk, clr
  Multiplexer #(.select(2), .width(12)) multiplexer_1 (
    .in0(R0), .in1(R1), .in2(R2), .in3(R3), .out(SAIDA_1), .sel(RS1));
  Multiplexer #(.select(2), .width(12)) multiplexer_2 (
    .in0(R0), .in1(R1), .in2(R2), .in3(R3), .out(SAIDA_2), .sel(RS2));
endmodule

module BranchControl (
  input  [11:0] RS1,
  input  [11:0] RS2,
  output BRANCH
);

  wire comparator_1_eq, comparator_2_eq, comparator_3_eq, comparator_3_gt, comparator_4_lt, not_1_out,
       or_1_out;
  wire [1:0] BranchType;

  Comparator #(.width(12)) comparator_1 (.a(RS1), .b(RS2), .eq(comparator_1_eq));  // open: gt, lt
  Comparator #(.width(12)) comparator_2 (.a(RS1), .b(RS2), .eq(comparator_2_eq));  // open: gt, lt
  Comparator #(.width(12)) comparator_3 (.a(RS1), .b(RS2), .gt(comparator_3_gt), .eq(comparator_3_eq));  // open: lt
  Comparator #(.width(12)) comparator_4 (.a(RS1), .b(RS2), .lt(comparator_4_lt));  // open: gt, eq
  not not_1 (not_1_out, comparator_2_eq);
  or or_1 (or_1_out, comparator_3_gt, comparator_3_eq);
  Multiplexer #(.select(2)) multiplexer_1 (
    .in0(comparator_1_eq), .in1(not_1_out), .in2(or_1_out), .in3(comparator_4_lt), .out(BRANCH),
    .sel(BranchType));
endmodule
